# Fritzing sketch schéma_projet (saved by Fritzing 0.9.3b)
breadboards: 1

parts:
  U1 = NodeMCU V1.0
  R1 = Rotary Potentiometer (Small) [maximum_resistance=100kΩ package=THT]
  LED1 = LED - 5mm [color="Red (633nm)" package="5 mm [THT]"]
  R2 = Resistor [tolerance=±5% resistance=220 package=THT]
  LED2 = LED - 5mm [color="Red (633nm)" package="5 mm [THT]"]
  R3 = Resistor [tolerance=±5% resistance=220 package=THT]
  LED3 = LED - 5mm [color="Red (633nm)" package="5 mm [THT]"]
  R4 = Resistor [tolerance=±5% resistance=220 package=THT]
  LED4 = LED - 5mm [color="Red (633nm)" package="5 mm [THT]"]
  R5 = Resistor [tolerance=±5% resistance=220 package=THT]
  LED5 = LED - 5mm [color="Red (633nm)" package="5 mm [THT]"]
  R6 = Resistor [tolerance=±5% resistance=220 package=THT]
  M1 = DC Motor  # not connected

nets:
  N1: U1.D1, LED1.cathode
  N2: U1.D2, LED2.cathode
  N3: U1.D3, LED3.cathode
  N4: U1.D4, LED4.cathode
  N5: U1.3V3, R1.leg2, R2.Pin_0, R3.Pin_0, R4.Pin_0, R5.Pin_0, R6.Pin_0
  N6: U1.GND, R1.leg1
  N7: U1.D5, LED5.cathode
  N8: U1.A0, R1.wiper
  N9: LED1.anode, R2.Pin_1
  N10: LED2.anode, R3.Pin_1
  N11: LED3.anode, R4.Pin_1
  N12: LED4.anode, R5.Pin_1
  N13: LED5.anode, R6.Pin_1

custom parts:
  NodeMCU V1.0: ESP8266 based NodeMCU
